# Fritzing sketch 2025 FRC 2491 Subsystem Diagram (saved by Fritzing 0.9.3b)

parts:
  BLDC1 = REV NEO 550 BLDC Motor [part_number=REV-21-1651]
  BLDC3 = REV NEO 550 BLDC Motor [part_number=REV-21-1651]
  PDH1 = rev_pdh
  ctrl2 = rev_spark_max [part_number=rev-11-2158]
  ctrl3 = rev_spark_max [part_number=rev-11-2158]
  BLDC4 = REV NEO 550 BLDC Motor [part_number=REV-21-1651]
  ctrl4 = rev_spark_max [part_number=rev-11-2158]
  Part1 = WCP_Kraken_X60 [part_number=19-708850]
  BLDC5 = CTRE Falcon 500 [part_number=19-708850]
  BLDC6 = CTRE Falcon 500 [part_number=19-708850]
  BLDC8 = REV NEO 550 BLDC Motor [part_number=REV-21-1651]
  ctrl5 = rev_spark_max [part_number=rev-11-2158]
  BLDC9 = REV NEO 550 BLDC Motor [part_number=REV-21-1651]
  ctrl7 = rev_spark_max [part_number=rev-11-2158]
  BLDC10 = REV NEO 550 BLDC Motor [part_number=REV-21-1651]
  ctrl8 = rev_spark_max [part_number=rev-11-2158]

nets:
  N1: BLDC1.A, ctrl3.connector18
  N2: BLDC1.B, ctrl3.connector2
  N3: BLDC1.C, ctrl3.connector3
  N4: BLDC1.GND, ctrl3.connector19
  N5: BLDC3.A, ctrl2.connector18
  N6: BLDC3.B, ctrl2.connector2
  N7: BLDC3.C, ctrl2.connector3
  N8: BLDC3.EA, ctrl2.connector19
  N9: PDH1.connector10, ctrl2.connector0
  N10: PDH1.connector11, ctrl2.connector1
  N11: PDH1.connector12, ctrl4.connector0
  N12: PDH1.connector13, ctrl4.connector1
  N13: PDH1.connector14, ctrl3.connector0
  N14: PDH1.connector15, ctrl3.connector1
  N15: PDH1.connector16, Part1.Vin+
  N16: PDH1.connector17, Part1.Vin-
  N17: PDH1.connector20, BLDC6.Vin+
  N18: PDH1.connector21, BLDC6.Vin-
  N19: PDH1.connector22, BLDC5.Vin+
  N20: PDH1.connector23, BLDC5.Vin-
  N21: PDH1.connector24, ctrl7.connector0
  N22: PDH1.connector25, ctrl7.connector1
  N23: PDH1.connector26, ctrl5.connector1
  N24: PDH1.connector27, ctrl5.connector0
  N25: PDH1.connector28, ctrl8.connector1
  N26: PDH1.connector29, ctrl8.connector0
  N27: BLDC4.A, ctrl4.connector18
  N28: BLDC4.B, ctrl4.connector2
  N29: BLDC4.C, ctrl4.connector3
  N30: BLDC4.EA, ctrl4.connector19
  N31: BLDC8.A, ctrl5.connector18
  N32: BLDC8.B, ctrl5.connector2
  N33: BLDC8.C, ctrl5.connector3
  N34: BLDC8.GND, ctrl5.connector19
  N35: BLDC9.A, ctrl7.connector18
  N36: BLDC9.B, ctrl7.connector2
  N37: BLDC9.C, ctrl7.connector3
  N38: BLDC9.GND, ctrl7.connector19
  N39: BLDC10.A, ctrl8.connector18
  N40: BLDC10.B, ctrl8.connector2
  N41: BLDC10.C, ctrl8.connector3
  N42: BLDC10.GND, ctrl8.connector19

notes:
  pretend there is a 30 amp here
  angled funnel 550
  straight funnel 550
  Funnel Dropper 550
  Climber

custom parts:
  REV NEO 550 BLDC Motor: The REV NEO 550 Brushless Motor is the newest member in the NEO family of brushless motors. Its output power and small size are specifically designed to make NEO 550 the perfect motor for intakes and other non-drivetrain robot mechanisms. Mounting holes and pilot match a standard 550 series motor, making it natively mount to many existing off-the-shelf gearboxes.
  WCP_Kraken_X60: The Kraken X60 is a brushless motor developed by WestCoast Products that has been designed to withstand the rigors of the FIRST Robotics Competition.
  CTRE Falcon 500: The Falcon 500 powered by Talon FX is a brushless motor with an integrated motor controller and high-resolution encoder, custom designed specifically for the FIRST Robotics Competition, through a collaboration between Cross the Road Electronics and VEX Robotics.
